# Fritzing sketch SD card (saved by Fritzing 0.9.3b)
breadboards: 1

parts:
  Part1 = Arduino Uno (Rev3)
  S1 = Pushbutton [package="[THT]"]
  R2 = Resistor [tolerance=±5% resistance=10k package=THT]
  R3 = Trimmer Potentiometer [maximum_resistance=10kΩ package=THT]  # not connected
  microSD_Transflash1 = SparkFun - microSD Transflash

nets:
  N1: Part1.D8, microSD_Transflash1.CS
  N2: Part1.D9_PWM, microSD_Transflash1.CD
  N3: Part1.D11_PWM/MOSI, microSD_Transflash1.DI
  N4: Part1.D12/MISO, microSD_Transflash1.DO
  N5: Part1.D13/SCK, microSD_Transflash1.SCK
  N6: Part1.D4, S1.Pin_3, S1.Pin_4, R2.Pin_1
  5V: Part1.5V, S1.Pin_1, S1.Pin_2, R2.Pin_0, microSD_Transflash1.VCC
  GND: Part1.GND, microSD_Transflash1.GND
